# Fritzing sketch 01_button_10kpulldown (saved by Fritzing 0.9.10b)
circuit board: 6.85431cm x 5.32372cm

parts:
  Part1 = Arduino Uno (Rev3)
  R1 = Resistor [tolerance=±5% power=0.25 resistance=10k package=THT]
  S1 = Pushbutton [package="[THT]"]

nets:
  N1: Part1.GND, R1.Pin_0
  N2: Part1.D7, R1.Pin_1, S1.Pin_3, S1.Pin_4
  N3: Part1.5V, S1.Pin_1, S1.Pin_2

// code stored in the sketch: 01_button_10kpulldown.ino

int pin = 7; // declare pin number for digital read


int buttonVal = 0; // declare variable to store digital read value



void setup() {

  pinMode(pin, INPUT); // set pin as an input

  Serial.begin(9600); // begin serial so we can communicate with the Arduino over USB

}



void loop() {

  buttonVal = digitalRead(pin); // digital read pin and assign the reading to buttonVal

  Serial.print(buttonVal); // print the button value in a new line in serial



  delay(50); // pause loop here for 50ms

}
