# Fritzing sketch 02_button_internal_pullup (saved by Fritzing 0.9.10b)
circuit board: 6.88566cm x 5.36311cm

parts:
  Part1 = Arduino Uno (Rev3)
  S1 = Pushbutton [package="[THT]"]

nets:
  N1: Part1.D7, S1.Pin_3, S1.Pin_4
  N2: Part1.GND, S1.Pin_2

// code stored in the sketch: 01_button_10kpulldown.ino

int pin = 7; // declare pin number for digital read


int buttonVal = 0; // declare variable to store digital read value



void setup() {

  pinMode(pin, INPUT); // set pin as an input

  Serial.begin(9600); // begin serial so we can communicate with the Arduino over USB

}



void loop() {

  buttonVal = digitalRead(pin); // digital read pin and assign the reading to buttonVal

  Serial.print(buttonVal); // print the button value in a new line in serial



  delay(50); // pause loop here for 50ms

}
