# Fritzing sketch 03_pressure_sensor (saved by Fritzing 0.9.10b)
circuit board: 6.88566cm x 5.36311cm

parts:
  Part1 = Arduino Uno (Rev3)
  J1 = Basic Force Sensing Resistor (FSR) [package=THT]
  R1 = Resistor [tolerance=±5% power=0.25 resistance=10k package=THT]

nets:
  N1: Part1.A0, J1.pin_0, R1.Pin_1
  N2: Part1.5V, J1.pin_1
  N3: Part1.GND, R1.Pin_0

// code stored in the sketch: 03_pressure_sensor.ino

int pin = A0; // declare pin number for digital read


int analogVal = 0; // declare variable to store digital read value



void setup() {

  pinMode(pin, INPUT); // set pin as an input

  Serial.begin(9600); // begin serial so we can communicate with the Arduino over USB

}



void loop() {

  analogVal = analogRead(pin); // digital read pin and assign the reading to buttonVal

  Serial.println(analogVal); // print the button value in a new line in serial



  delay(50); // pause loop here for 50ms

}
