# Fritzing sketch 05_touch_4pads (saved by Fritzing 0.9.10b)
circuit board: 6.86122cm x 5.6528cm

parts:
  Part1 = Arduino Uno (Rev3)
  R1 = Resistor [tolerance=±5% power=0.25 resistance=1M package=THT]
  R2 = Resistor [tolerance=±5% power=0.25 resistance=1M package=THT]
  J2 = STARBOARD_GND [package=starboard_ground_wide]
  J1 = STARBOARD_GND [package=starboard_ground_wide]
  R3 = Resistor [tolerance=±5% power=0.25 resistance=1M package=THT]
  J3 = STARBOARD_GND [package=starboard_ground_wide]
  R4 = Resistor [tolerance=±5% power=0.25 resistance=1M package=THT]
  J4 = STARBOARD_GND [package=starboard_ground_wide]

nets:
  N1: Part1.D2, R1.Pin_1, J1.MOUNT
  N2: Part1.D3_PWM, R2.Pin_1, J2.MOUNT
  N3: Part1.D4, R3.Pin_1, J3.MOUNT
  N4: Part1.D5_PWM, R4.Pin_1, J4.MOUNT
  N5: Part1.D6_PWM, R1.Pin_0, R2.Pin_0, R3.Pin_0, R4.Pin_0
